# Fritzing sketch testBoard (saved by Fritzing 0.9.3b)
breadboards: 1

parts:
  U1 = PCF8575C [package=so-24dw]
  Part1 = Arduino Uno (Rev3)
  LED1 = LED - 5mm [color="Red (633nm)" current=0.030 package="5 mm [THT]"]
  LED2 = LED - 5mm [color="Red (633nm)" current=0.030 package="5 mm [THT]"]
  LED3 = LED - 5mm [color="Red (633nm)" current=0.030 package="5 mm [THT]"]
  LED4 = LED - 5mm [color="Red (633nm)" current=0.030 package="5 mm [THT]"]
  LED5 = LED - 5mm [color="Red (633nm)" current=0.030 package="5 mm [THT]"]
  LED6 = LED - 5mm [color="Red (633nm)" current=0.030 package="5 mm [THT]"]
  LED7 = LED - 5mm [color="Red (633nm)" current=0.030 package="5 mm [THT]"]
  LED8 = LED - 5mm [color="Red (633nm)" current=0.030 package="5 mm [THT]"]
  R1 = Resistor [tolerance=±5% resistance=220 power=0.25 package=THT]
  R2 = Resistor [tolerance=±5% resistance=220 power=0.25 package=THT]
  R3 = Resistor [tolerance=±5% resistance=220 power=0.25 package=THT]
  R4 = Resistor [tolerance=±5% resistance=220 power=0.25 package=THT]
  R5 = Resistor [tolerance=±5% resistance=220 power=0.25 package=THT]
  R6 = Resistor [tolerance=±5% resistance=220 power=0.25 package=THT]
  R7 = Resistor [tolerance=±5% resistance=220 power=0.25 package=THT]
  R8 = Resistor [tolerance=±5% resistance=220 power=0.25 package=THT]
  R9 = Resistor [tolerance=±5% resistance=220 power=0.25 package=THT]
  R10 = Resistor [tolerance=±5% resistance=220 power=0.25 package=THT]
  R11 = Resistor [tolerance=±5% resistance=220 power=0.25 package=THT]
  R12 = Resistor [tolerance=±5% resistance=220 power=0.25 package=THT]
  R13 = Resistor [tolerance=±5% resistance=220 power=0.25 package=THT]
  R14 = Resistor [tolerance=±5% resistance=220 power=0.25 package=THT]
  R15 = Resistor [tolerance=±5% resistance=220 power=0.25 package=THT]
  R16 = Resistor [tolerance=±5% resistance=220 power=0.25 package=THT]
  LED9 = LED - 5mm [color="Red (633nm)" current=0.030 package="5 mm [THT]"]
  LED10 = LED - 5mm [color="Red (633nm)" current=0.030 package="5 mm [THT]"]
  LED11 = LED - 5mm [color="Red (633nm)" current=0.030 package="5 mm [THT]"]
  LED12 = LED - 5mm [color="Red (633nm)" current=0.030 package="5 mm [THT]"]
  LED13 = LED - 5mm [color="Red (633nm)" current=0.030 package="5 mm [THT]"]
  LED14 = LED - 5mm [color="Red (633nm)" current=0.030 package="5 mm [THT]"]  # not connected
  LED15 = LED - 5mm [color="Red (633nm)" current=0.030 package="5 mm [THT]"]  # not connected
  LED16 = LED - 5mm [color="Red (633nm)" current=0.030 package="5 mm [THT]"]

nets:
  N1: U1.INT, Part1.D2
  N2: U1.PO0, LED8.cathode, LED8.anode, R1.Pin_0
  N3: U1.PO1, LED7.cathode, LED7.anode, R2.Pin_0
  N4: U1.PO2, LED6.cathode, LED6.anode, R3.Pin_0
  N5: U1.PO3, LED5.cathode, LED5.anode, R8.Pin_0
  N6: U1.PO4, LED4.cathode, LED4.anode, R4.Pin_0
  N7: U1.PO5, LED3.cathode, LED3.anode, R5.Pin_0
  N8: U1.PO6, LED2.cathode, LED2.anode, R6.Pin_0
  N9: U1.PO7, LED1.cathode, LED1.anode, R7.Pin_0
  GND: U1.GND, Part1.GND
  N10: U1.P10, R16.Pin_1, LED16.cathode, LED16.anode
  N11: U1.P11, R15.Pin_1
  N12: U1.P12, R14.Pin_1
  N13: U1.P13, R13.Pin_1, LED13.cathode, LED13.anode
  N14: U1.P14, R12.Pin_1, LED12.cathode, LED12.anode
  N15: U1.P15, R11.Pin_1, LED11.cathode, LED11.anode
  N16: U1.P16, R10.Pin_1, LED10.cathode, LED10.anode
  N17: U1.P17, R9.Pin_1, LED9.cathode, LED9.anode
  N18: U1.SCL, Part1.A5/SCL
  N19: U1.SDA, Part1.A4/SDA
  VCC: U1.VCC, Part1.5V, R1.Pin_1, R2.Pin_1, R3.Pin_1, R4.Pin_1, R5.Pin_1, R6.Pin_1, R7.Pin_1, R8.Pin_1, R9.Pin_0, R10.Pin_0, R11.Pin_0, R12.Pin_0, R13.Pin_0, R14.Pin_0, R15.Pin_0, R16.Pin_0

notes:
  SDA
  SCL
  INT
  P0
  P1
